// Logisim project alu_registry.circ as structural Verilog: 1 circuit, main circuit alu_registry
module alu_registry (
  input  [3:0] Rin1,
  input  [3:0] Rin2,
  input  [3:0] Rout,
  input  [7:0] REG_In,
  input  [3:0] Op,
  output Zero,
  output [7:0] REG_Out,
  output [7:0] ALU_Out
);

  wire [7:0] registry_1_sb;

  registry registry_1 (
    .slctB(Rin2), .slctA(Rin1), .C(REG_In), .slctC(Rout), .sA(REG_Out), .sB(registry_1_sb), .S7_1bit(Zero));
  ALU alu_1 (.A(REG_Out), .B(registry_1_sb), .slct(Op), .S(ALU_Out));  // open: Err
endmodule
