// Logisim project decode.circ as structural Verilog
module decode (
  input  [23:0] instru,
  input  We
);

  wire [3:0] decode_instru_1_slctop, decode_instru_1_slctrega, decode_instru_1_slctregb,
       decode_instru_1_slctregwrite;
  wire [7:0] data_path_1_s;
  wire [23:0] registry_24bits_1_s;

  registry_24bits registry_24bits_1 (.instru(instru), .We(We), .S(registry_24bits_1_s));
  decode_instru decode_instru_1 (
    .instru(registry_24bits_1_s), .slctOp(decode_instru_1_slctop), .slctRegA(decode_instru_1_slctrega),
    .slctRegB(decode_instru_1_slctregb), .slctRegWrite(decode_instru_1_slctregwrite));
  data_path data_path_1 (
    .slctB(decode_instru_1_slctregb), .slctA(decode_instru_1_slctrega), .C(data_path_1_s),
    .slctOP(decode_instru_1_slctop), .slctC(decode_instru_1_slctregwrite), .S(data_path_1_s));  // open: sA, out_8, S7_1bit
endmodule

module decode_instru (
  input  [23:0] instru,
  output [3:0] slctOp,
  output [3:0] slctRegA,
  output [3:0] slctRegB,
  output [3:0] slctRegWrite
);

  Multiplexer #(.select(4), .width(4)) multiplexer_1 (
    .in0(instru[11:8]), .in1(instru[11:8]), .in2(instru[11:8]), .in3(instru[11:8]), .in4(instru[11:8]),
    .in5(instru[11:8]), .in6(instru[11:8]), .in7(instru[11:8]), .in8(instru[11:8]), .in9(instru[11:8]),
    .in10(instru[11:8]), .in11(instru[11:8]), .in12(4'b0000), .in13(4'b0000), .in14(4'b0000), .in15(4'b0000),
    .out(slctRegB), .sel(slctOp));
  type_op_to_slctOp type_op_to_slctop_1 (.typee(instru[23:20]), .operation(instru[19:16]), .slcOp(slctOp));
  Multiplexer #(.select(4), .width(4)) multiplexer_2 (
    .in0(instru[3:0]), .in1(instru[3:0]), .in2(instru[3:0]), .in3(instru[3:0]), .in4(instru[3:0]),
    .in5(instru[3:0]), .in6(instru[3:0]), .in7(instru[3:0]), .in8(4'b1000), .in9(4'b1000), .in10(4'b1000),
    .in11(4'b1000), .in12(4'b1000), .in13(instru[3:0]), .in14(instru[3:0]), .in15(instru[3:0]),
    .out(slctRegWrite), .sel(slctOp));

  assign slctRegA = instru[15:12];
endmodule

module type_op_to_slctOp (
  input  [3:0] typee,
  input  [3:0] operation,
  output [3:0] slcOp
);

  wire and_1_out, and_2_out, and_3_out, and_4_out, and_5_out, and_6_out, and_7_out, and_8_out, not_2_out,
       not_3_out, not_4_out;

  not not_1 (slcOp[3], typee[0]);
  not not_2 (not_2_out, operation[3]);
  not not_3 (not_3_out, operation[1]);
  not not_4 (not_4_out, operation[0]);
  and and_1 (and_1_out, typee[0], not_2_out);
  and and_2 (and_2_out, slcOp[3], operation[3]);
  and and_3 (and_3_out, slcOp[3], not_2_out, not_3_out);
  and and_4 (and_4_out, operation[2], not_3_out);
  and and_5 (and_5_out, typee[0], operation[1]);
  and and_6 (and_6_out, typee[0], operation[0]);
  and and_7 (and_7_out, not_2_out, operation[2]);
  and and_8 (and_8_out, slcOp[3], not_4_out);
  or or_1 (slcOp[2], and_1_out, and_2_out);
  or or_2 (slcOp[1], and_3_out, and_4_out, and_5_out);
  or or_3 (slcOp[0], and_6_out, and_7_out, and_8_out);
endmodule
