// Logisim project squidcpu.circ as structural Verilog: 1 circuit, main circuit main
module main (
);

  wire alu_registry_1_zero, undriven, undriven_4;
  wire [1:0] undriven_3;
  wire [3:0] undriven_5, undriven_6, undriven_7, undriven_8;
  wire [7:0] alu_registry_1_alu_out, alu_registry_1_reg_out, pc_1_addr_code, pc_1_addr_data, pc_1_reg_in,
       ram_data_1_stor_out, undriven_2;
  wire [23:0] rom_instru_1_instru_out;

  ram_data ram_data_1 (
    .stor_addr(pc_1_addr_data), .We(undriven_4), .stor_in(alu_registry_1_reg_out),
    .stor_out(ram_data_1_stor_out));
  rom_instru rom_instru_1 (.addr(pc_1_addr_code), .instru_out(rom_instru_1_instru_out));
  // fetch_decode fetch_decode_1: pin names not known; wires that end beside it: rom_instru_1_instru_out
  pc pc_1 (
    .RAM(ram_data_1_stor_out), .ALU(alu_registry_1_alu_out), .jmp(undriven), .addr8(undriven_2),
    .slctREG_IN(undriven_3), .addr_data(pc_1_addr_data), .REG_IN(pc_1_reg_in), .addr_code(pc_1_addr_code));
  alu_registry alu_registry_1 (
    .Rin2(undriven_6), .Rout(undriven_7), .REG_In(pc_1_reg_in), .Rin1(undriven_8), .Op(undriven_5),
    .Zero(alu_registry_1_zero), .REG_Out(alu_registry_1_reg_out), .ALU_Out(alu_registry_1_alu_out));
endmodule
